# Fritzing sketch Ejemplo10-Cap4 (saved by Fritzing 0.9.3b)
breadboards: 1

parts:
  Componente1 = EmDroidV2.0
  JACK1 = 2.1mm Barrel Jack with Terminal Block  # not connected
  R1 = Resistor [tolerance=±5% resistance=10k package="1206 [SMD]"]
  OLED1 = OLED 128x64 I2C Monochrome Display GND-VDD
  R2 = Resistor [tolerance=±5% resistance=10k package="1206 [SMD]"]
  S1 = Pushbutton [package="[SMD]"]
  R3 = Resistor [tolerance=±5% resistance=10k package="1206 [SMD]"]

nets:
  N1: Componente1.PB0_(12), S1.Pin_1, S1.Pin_2, R3.Pin_0
  N2: Componente1.PC4_(27), OLED1.SDA, R2.Pin_1
  N3: Componente1.PC5_(28), R1.Pin_1, OLED1.SCK
  N4: Componente1.VCC_(5V), R1.Pin_0, OLED1.VDD, R2.Pin_0, S1.Pin_3, S1.Pin_4
  GND: Componente1.GND, OLED1.GND, R3.Pin_1

custom parts:
  OLED 128x64 I2C Monochrome Display GND-VDD: OLED 128x64 I2C Monochrome Display. Note: there are two variants of this part, this one is the GND VDD SCK SDA variant. The other is VDD GND SCK SDA. Make sure you select the part that matches your module as using the incorrect part will probably destroy your module! In addition the mounting holes are marked on silkscreen but not by default drilled. If you want drilled mounting holes, copy a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
