# Fritzing sketch Ejemplo11-Cap4 (saved by Fritzing 0.9.3b)
breadboards: 1

parts:
  Componente1 = EmDroidV2.0
  JACK1 = 2.1mm Barrel Jack with Terminal Block  # not connected
  R1 = Resistor [tolerance=±5% resistance=10k package="1206 [SMD]"]
  OLED1 = OLED 128x64 I2C Monochrome Display GND-VDD
  R2 = Resistor [tolerance=±5% resistance=10k package="1206 [SMD]"]
  Componente2 = KY-033 Tracing Black White Line Hunting Sensor Module For Arduino

nets:
  N1: Componente1.PB0_(12), Componente2.S
  N2: Componente1.PC4_(27), OLED1.SDA, R2.Pin_1
  N3: Componente1.PC5_(28), R1.Pin_1, OLED1.SCK
  N4: Componente1.VCC_(5V), R1.Pin_0, OLED1.VDD, R2.Pin_0, Componente2.V+
  GND: Componente1.GND, OLED1.GND, Componente2.GND

custom parts:
  OLED 128x64 I2C Monochrome Display GND-VDD: OLED 128x64 I2C Monochrome Display. Note: there are two variants of this part, this one is the GND VDD SCK SDA variant. The other is VDD GND SCK SDA. Make sure you select the part that matches your module as using the incorrect part will probably destroy your module! In addition the mounting holes are marked on silkscreen but not by default drilled. If you want drilled mounting holes, copy a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
  KY-033 Tracing Black White Line Hunting Sensor Module For Arduino: Tracing Black White Line Hunting Sensor Module For Arduino Description: This is KY-033 tracking sensor. The KY-033 measures the intensity of infrared radiation and delivers it as an analog output voltage. Features: Operating voltage: 2.5 - 12V(cannot over12V) working current: 18mA-20mA at 5V Enhanced accuracy Documents: http://www.vishay.com/docs/83760/tcrt5000.pdf
