# Fritzing sketch Ejemplo13-Cap5 (saved by Fritzing 0.9.3b)
breadboards: 1

parts:
  Componente1 = EmDroidV2.0
  JACK1 = 2.1mm Barrel Jack with Terminal Block  # not connected
  OLED1 = OLED 128x64 I2C Monochrome Display GND-VDD
  A1 = GY-SHT30 Breakout
  LED1 = smd LED [color="Red (633nm)" package="1206 [SMD]"]
  R1 = Resistor [tolerance=±5% resistance=220 package="1206 [SMD]"]

nets:
  N1: Componente1.PC4_(27), OLED1.SDA, A1.Pin_4
  N2: Componente1.PC5_(28), OLED1.SCK, A1.Pin_3
  N3: Componente1.PD2_(32), LED1.anode
  N4: Componente1.VCC_(5V), OLED1.VDD, A1.Pin_1
  GND: Componente1.GND, OLED1.GND, A1.Pin_2, R1.Pin_1
  N5: LED1.cathode, R1.Pin_0

custom parts:
  OLED 128x64 I2C Monochrome Display GND-VDD: OLED 128x64 I2C Monochrome Display. Note: there are two variants of this part, this one is the GND VDD SCK SDA variant. The other is VDD GND SCK SDA. Make sure you select the part that matches your module as using the incorrect part will probably destroy your module! In addition the mounting holes are marked on silkscreen but not by default drilled. If you want drilled mounting holes, copy a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
