# Fritzing sketch Ejemplo14-Cap5 (saved by Fritzing 0.9.3b)
breadboards: 1

parts:
  Componente1 = EmDroidV2.0
  JACK1 = 2.1mm Barrel Jack with Terminal Block  # not connected
  Componente2 = LCD1602-I2C
  A1 = GY-BMP280 Breakout
  LED1 = LED - 5mm [color="Red (633nm)" package="5 mm [THT]"]
  R1 = Resistor [tolerance=±5% resistance=220 package="0603 [SMD]"]

nets:
  N1: Componente1.PD3_(1), LED1.anode
  N2: Componente1.PC4_(27), Componente2.SDA, A1.Pin_4
  N3: Componente1.PC5_(28), Componente2.SCL, A1.Pin_3
  N4: Componente1.VCC_(5V), Componente2.VCC, A1.Pin_1
  GND: Componente1.GND, Componente2.GND, A1.Pin_2, A1.Pin_6, R1.Pin_1
  N5: LED1.cathode, R1.Pin_0

notes:
  Alarma (PD3)
  BME/P280

custom parts:
  LCD1602-I2C: A standard character display, usually with 2x16 characters. Comes in many colors with LCM1602 IIC attached.
