# Fritzing sketch Ejemplo16-Cap5 (saved by Fritzing 0.9.3b)
breadboards: 1

parts:
  Componente1 = EmDroidV2.0
  JACK1 = 2.1mm Barrel Jack with Terminal Block  # not connected
  A1 = GY-SHT30 Breakout
  Componente2 = LCD1602-I2C

nets:
  N1: Componente1.PC4_(27), A1.Pin_4, Componente2.SDA
  N2: Componente1.PC5_(28), A1.Pin_3, Componente2.SCL
  N3: Componente1.VCC_(5V), A1.Pin_1, Componente2.VCC
  GND: Componente1.GND, A1.Pin_2, Componente2.GND

custom parts:
  LCD1602-I2C: A standard character display, usually with 2x16 characters. Comes in many colors with LCM1602 IIC attached.
