# Fritzing sketch Ejemplo17-Cap5 (saved by Fritzing 0.9.3b)
breadboards: 1

parts:
  Componente1 = EmDroidV2.0
  JACK1 = 2.1mm Barrel Jack with Terminal Block  # not connected
  Componente2 = LCD1602-I2C
  LED1 = smd LED [color="Red (633nm)" package="0603 [SMD]"]
  R1 = Resistor [tolerance=±5% resistance=220 package="2010 [SMD]"]

nets:
  N1: Componente1.PB0_(12), LED1.anode
  N2: Componente1.PC4_(27), Componente2.SDA
  N3: Componente1.PC5_(28), Componente2.SCL
  N4: Componente2.GND, R1.Pin_1
  N5: LED1.cathode, R1.Pin_0

custom parts:
  LCD1602-I2C: A standard character display, usually with 2x16 characters. Comes in many colors with LCM1602 IIC attached.
