# Fritzing sketch Ejemplo20-Cap6 (saved by Fritzing 0.9.3b)
breadboards: 1

parts:
  LCD1 = LCD screen
  R2 = Resistor [tolerance=±5% resistance=1k package="0603 [SMD]"]
  Componente1 = EmDroidV2.0
  R3 = Resistor [tolerance=±5% resistance=220 package="0603 [SMD]"]
  JACK1 = 2.1mm Barrel Jack with Terminal Block  # not connected
  hc-sr1 = hc-sr04
  SERVO1 = Tower Pro SG90 servo [part_number=101246]

nets:
  GND: LCD1.VSS, LCD1.R/W, R2.Pin_0, Componente1.GND, R3.Pin_0, hc-sr1.GND, SERVO1.GND
  VDD: LCD1.VDD, LCD1.LED+, Componente1.VCC_(5V), hc-sr1.VCC, SERVO1.+5V
  N1: LCD1.V0, R2.Pin_1
  N2: LCD1.RS, Componente1.PD4_(2)
  N3: LCD1.E, Componente1.PD6_(10)
  N4: LCD1.DB4, Componente1.PC0_(23)
  N5: LCD1.DB5, Componente1.PC1_(24)
  N6: LCD1.DB6, Componente1.PC2_(25)
  N7: LCD1.DB7, Componente1.PC3_(26)
  N8: LCD1.LED-, R3.Pin_1
  N9: Componente1.PB0_(12), hc-sr1.Echo
  N10: Componente1.PB1_(13), hc-sr1.Trig
  N11: Componente1.PB3_(15), SERVO1.Signal

custom parts:
  Tower Pro SG90 servo: Original file by John De Cristofaro http://www.adafruit.com/products/1449 Adafruit Feedback Servo (Small) Edited by: e-radionica.com 28/9/2015
