# Fritzing sketch Ejemplo21-Cap6 (saved by Fritzing 0.9.3b)
breadboards: 1

parts:
  Componente1 = EmDroidV2.0
  S1 = Pololu QTR-8 Reflectabce Sensor array [package=THT]
  L298N1 = Mini L298N H-Bridge [package=Module]
  BAT1 = Battery Holders [package=lipo-1100mAh]
  M1 = Getriebemotor
  M2 = Getriebemotor

nets:
  N1: Componente1.PB1_(13), L298N1.IN1
  N2: Componente1.PB2_(14), L298N1.IN3
  N3: Componente1.PC0_(23), S1.pin10
  N4: Componente1.PC1_(24), S1.pin9
  N5: Componente1.PC2_(25), S1.pin8
  N6: Componente1.PC3_(26), S1.pin7
  N7: Componente1.VCC_(5V), S1.pin2
  GND: Componente1.GND, S1.pin1, S1.pin15, S1.pin21, L298N1.GND, L298N1.IN2, L298N1.IN4, BAT1.-
  N8: L298N1.MA+, M1.pin_1
  N9: L298N1.MA-, M1.pin_2
  N10: L298N1.MB+, M2.pin_1
  N11: L298N1.MB-, M2.pin_2
  N12: L298N1.VCC, BAT1.+

notes:
  Motor Derecho
  Motor Izquierdo
  MX1508 (controlador de motor DC)
  Arreglo de sensores qtr-8rc
  Batería LiPo 7.4V@1100mAh

custom parts:
  Mini L298N H-Bridge: Mini dual H-bridge motor driver module based on L298N
