# Fritzing sketch Ejemplo2SensorInfrarrojo-Cap3 (saved by Fritzing 0.9.3b)
breadboards: 1

parts:
  Mod1 = KY-032 IR Obstacle Avoidance Sensor Module [package="Breakout board"]
  Componente1 = EmDroidV2.0
  JACK1 = 2.1mm Barrel Jack with Terminal Block  # not connected
  LED1 = LED - 5mm [color="Red (633nm)" package="5 mm [THT]"]
  LED2 = LED - 5mm [color="Green (565nm)" package="5 mm [THT]"]
  R1 = Resistor [tolerance=±5% resistance=220 package=THT]
  R2 = Resistor [tolerance=±5% resistance=220 package=THT]

nets:
  GND: Mod1.GND, Componente1.GND, R1.Pin_1, R2.Pin_1
  N1: Mod1.+, Componente1.VCC_(5V)
  N2: Mod1.out, Componente1.PD0_(30)
  N3: Componente1.PD1_(31), LED1.anode
  N4: Componente1.PD2_(32), LED2.anode
  N5: LED1.cathode, R1.Pin_0
  N6: LED2.cathode, R2.Pin_0

custom parts:
  KY-032 IR Obstacle Avoidance Sensor Module: KY-032 Infrared Obstacle Avoidance Sensor. Distance-adjustable, infrared proximity sensor designed for wheeled robots. Also known as AD-032.
