# Fritzing sketch Ejemplo2SensorInfrarrojoIndustrial-Cap3 (saved by Fritzing 0.9.3b)
breadboards: 1

parts:
  Componente1 = EmDroidV2.0
  JACK1 = 2.1mm Barrel Jack with Terminal Block  # not connected
  LED1 = LED - 5mm [color="Red (633nm)" package="5 mm [THT]"]
  LED2 = LED - 5mm [color="Green (565nm)" package="5 mm [THT]"]
  R1 = Resistor [tolerance=±5% resistance=220 package=THT]
  R2 = Resistor [tolerance=±5% resistance=220 package=THT]
  M1 = E18-D80NK_1 [package=THT]

nets:
  N1: Componente1.PD0_(30), M1.pin3
  N2: Componente1.PD1_(31), LED1.anode
  N3: Componente1.PD2_(32), LED2.anode
  N4: Componente1.VCC_(5V), M1.pin2
  N5: Componente1.GND, R1.Pin_1, R2.Pin_1, M1.pin1
  N6: LED1.cathode, R1.Pin_0
  N7: LED2.cathode, R2.Pin_0

custom parts:
  E18-D80NK_1: E18-D80NK Proximity Sensor module.
