# Fritzing sketch Ejemplo4-Cap3 (saved by Fritzing 0.9.3b)
breadboards: 1

parts:
  Componente1 = EmDroidV2.0
  JACK1 = 2.1mm Barrel Jack with Terminal Block  # not connected
  S1 = Pushbutton [package="[THT]"]
  S2 = Pushbutton [package="[THT]"]
  R1 = Resistor [tolerance=±5% resistance=10k package="2010 [SMD]"]
  R2 = Resistor [tolerance=±5% resistance=10k package="2010 [SMD]"]
  R3 = Resistor [tolerance=±5% resistance=220 package="2010 [SMD]"]
  LED2 = smd LED [color="Red (633nm)" package="0805 [SMD]"]
  LED3 = smd LED [color="Green (555nm)" package="0805 [SMD]"]
  R4 = Resistor [tolerance=±5% resistance=220 package="2010 [SMD]"]

nets:
  N1: Componente1.PB0_(12), LED2.anode
  N2: Componente1.PB1_(13), LED3.anode
  N3: Componente1.PD0_(30), S1.Pin_3, S1.Pin_4, R1.Pin_1
  N4: Componente1.PD1_(31), S2.Pin_3, S2.Pin_4, R2.Pin_1
  N5: Componente1.VCC_(5V), R1.Pin_0, R2.Pin_0
  N6: Componente1.GND, S1.Pin_1, S1.Pin_2, S2.Pin_1, S2.Pin_2, R3.Pin_1, R4.Pin_1
  N7: R3.Pin_0, LED2.cathode
  N8: LED3.cathode, R4.Pin_0

notes:
  PulsA
  PulsB
  Led1
  Led2
