# Fritzing sketch Ejemplo6-Cap3 (saved by Fritzing 0.9.3b)
breadboards: 1

parts:
  Mod1 = KY-032 IR Obstacle Avoidance Sensor Module [package="Breakout board"]
  Componente1 = EmDroidV2.0
  JACK1 = 2.1mm Barrel Jack with Terminal Block  # not connected
  R2 = Resistor [tolerance=±5% resistance=220 package=THT]
  LED1 = LED - 5mm [color="Red (633nm)" package="5 mm [THT]"]
  Q1 = NPN-Transistor [package="SOT-23 [SMD]"]
  M1 = DC Motor
  R3 = Resistor [tolerance=±5% resistance=1k package="0603 [SMD]"]
  A1 = YL-45

nets:
  GND: Mod1.GND, Componente1.GND, R2.Pin_1, Q1.2, A1.Pin_1
  N1: Mod1.+, Componente1.VCC_(5V)
  N2: Mod1.out, Componente1.PD0_(30)
  N3: Componente1.PD1_(31), R3.Pin_0
  N4: Componente1.PD2_(32), LED1.anode
  N5: R2.Pin_0, LED1.cathode
  N6: Q1.0, R3.Pin_1
  N7: Q1.1, M1.pin_2
  N8: M1.pin_1, A1.Pin_3, A1.Pin_4

notes:
  Fuente externa: las tierras (GND) de la fuente y EmDroid se "puentean" (unen).
  Motor DC
  Transistor NPN
  Voltaje para el motor

custom parts:
  KY-032 IR Obstacle Avoidance Sensor Module: KY-032 Infrared Obstacle Avoidance Sensor. Distance-adjustable, infrared proximity sensor designed for wheeled robots. Also known as AD-032.
  YL-45: 5.5*2.1mm DC Jack Socket Plug Power Supply Module DC Power Adapter Board.
