# Fritzing sketch Ejemplo7LCD4bits-Cap4 (saved by Fritzing 0.9.3b)
breadboards: 1

parts:
  LCD1 = LCD screen
  S1 = Pushbutton [package="[THT]"]
  R1 = Resistor [tolerance=±5% resistance=10k package="0603 [SMD]"]
  R2 = Resistor [tolerance=±5% resistance=1k package="0603 [SMD]"]
  Componente1 = EmDroidV2.0
  R3 = Resistor [tolerance=±5% resistance=220 package="0603 [SMD]"]
  JACK1 = 2.1mm Barrel Jack with Terminal Block  # not connected

nets:
  VSS: LCD1.VSS, LCD1.R/W, S1.Pin_1, S1.Pin_2, R2.Pin_0, Componente1.GND, R3.Pin_0
  N1: LCD1.VDD, LCD1.LED+, R1.Pin_0, Componente1.VCC_(5V)
  N2: LCD1.V0, R2.Pin_1
  N3: LCD1.RS, Componente1.PD4_(2)
  N4: LCD1.E, Componente1.PD6_(10)
  N5: LCD1.DB4, Componente1.PC0_(23)
  N6: LCD1.DB5, Componente1.PC1_(24)
  N7: LCD1.DB6, Componente1.PC2_(25)
  N8: LCD1.DB7, Componente1.PC3_(26)
  N9: LCD1.LED-, R3.Pin_1
  N10: S1.Pin_3, S1.Pin_4, R1.Pin_1, Componente1.PB0_(12)
