# Fritzing sketch Ejemplo7LCDI2C-Cap4 (saved by Fritzing 0.9.3b)
breadboards: 1

parts:
  S1 = Pushbutton [package="[THT]"]
  R1 = Resistor [tolerance=±5% resistance=10k package="0603 [SMD]"]
  Componente1 = EmDroidV2.0
  JACK1 = 2.1mm Barrel Jack with Terminal Block  # not connected
  Componente2 = LCD1602-I2C

nets:
  GND: S1.Pin_1, S1.Pin_2, Componente1.GND, Componente2.GND
  N1: S1.Pin_3, S1.Pin_4, R1.Pin_1, Componente1.PB0_(12)
  N2: R1.Pin_0, Componente1.VCC_(5V), Componente2.VCC
  N3: Componente1.PC4_(27), Componente2.SDA
  N4: Componente1.PC5_(28), Componente2.SCL

custom parts:
  LCD1602-I2C: A standard character display, usually with 2x16 characters. Comes in many colors with LCM1602 IIC attached.
