# Fritzing sketch Ejemplo8-Cap4 (saved by Fritzing 0.9.3b)
breadboards: 1

parts:
  Componente1 = EmDroidV2.0
  JACK1 = 2.1mm Barrel Jack with Terminal Block  # not connected
  Componente2 = LCD1602-I2C

nets:
  N1: Componente1.PC4_(27), Componente2.SDA
  N2: Componente1.PC5_(28), Componente2.SCL
  N3: Componente1.VCC_(5V), Componente2.VCC
  GND: Componente1.GND, Componente2.GND

custom parts:
  LCD1602-I2C: A standard character display, usually with 2x16 characters. Comes in many colors with LCM1602 IIC attached.
