# Fritzing sketch Ejemplo9-Cap4 (saved by Fritzing 0.9.3b)
breadboards: 1

parts:
  Componente1 = EmDroidV2.0
  JACK1 = 2.1mm Barrel Jack with Terminal Block  # not connected
  Componente2 = KY-033 Tracing Black White Line Hunting Sensor Module For Arduino
  Componente3 = LCD1602-I2C

nets:
  N1: Componente1.PB0_(12), Componente2.S
  N2: Componente1.PC4_(27), Componente3.SDA
  N3: Componente1.PC5_(28), Componente3.SCL
  N4: Componente1.VCC_(5V), Componente2.V+, Componente3.VCC
  GND: Componente1.GND, Componente2.GND, Componente3.GND

custom parts:
  KY-033 Tracing Black White Line Hunting Sensor Module For Arduino: Tracing Black White Line Hunting Sensor Module For Arduino Description: This is KY-033 tracking sensor. The KY-033 measures the intensity of infrared radiation and delivers it as an analog output voltage. Features: Operating voltage: 2.5 - 12V(cannot over12V) working current: 18mA-20mA at 5V Enhanced accuracy Documents: http://www.vishay.com/docs/83760/tcrt5000.pdf
  LCD1602-I2C: A standard character display, usually with 2x16 characters. Comes in many colors with LCM1602 IIC attached.
