# Fritzing sketch EsquemaCap2 (saved by Fritzing 0.9.3b)
breadboards: 1

parts:
  Componente1 = EmDroidV2.0
  R1 = Resistor [tolerance=±5% resistance=220 package="0402 [SMD]"]
  LED2 = smd LED [color="Red (633nm)" package="1206 [SMD]"]
  JACK1 = 2.1mm Barrel Jack with Terminal Block  # not connected

nets:
  N1: Componente1.PD3_(1), LED2.anode
  N2: Componente1.GND, R1.Pin_1
  N3: R1.Pin_0, LED2.cathode
